# Fritzing sketch L293D_Breadbord - 2 motors and ultrasonic-sensor (saved by Fritzing 1.0.4)
breadboards: 1

parts:
  IC1 = L293D [package=THT]
  Mod1 = Raspberry Pi 4B
  VCC1 = Battery block 9V [internal_resistance=0.1Ω]
  M1 = DC Motor [voltage_(max)=6V voltage_(min)=3V]
  M2 = DC Motor [voltage_(max)=6V voltage_(min)=3V]
  HC-SR04_Sensor_1 = HC-SR04 Ultrasonic Distance Sensor  # not connected

nets:
  N1: IC1.Enable_1, IC1.Enable_2, IC1.+V, Mod1.5V
  N2: IC1.In_1, Mod1.GPIO23
  N3: IC1.Out_1_(_Controlled_by_Enable_1_), M2.pin_2
  N4: IC1.0V, Mod1.GND, VCC1.-
  N5: IC1.Out_2_(_Controlled_by_Enable_1_), M2.pin_1
  N6: IC1.In_2, Mod1.GPIO24
  N7: IC1.+Vmotor, VCC1.+
  N8: IC1.In_3, Mod1.GPIO27
  N9: IC1.Out_3_(_Controlled_by_Enable_2_), M1.pin_2
  N10: IC1.Out_4_(_Controlled_by_Enable_2_), M1.pin_1
  N11: IC1.In_4, Mod1.GPIO22
